# Fritzing sketch Untitled Sketch (saved by Fritzing 0.9.3b)
breadboards: 1

parts:
  부품1 = Arduino Mega 2560 (Rev3)
  Keypad4x2 = Keypad Membran 4x4
  부품2 = NeoPixel Stick [part_number=1426]
  J1 = Basic Servo
  J2 = Basic Servo
  J3 = Basic Servo
  부품3 = RFID-RC522-v2
  J4 = Piezo Speaker
  S1 = H-Bridge with L298N
  F1 = Fan - Ventilador [package=THT]
  M1 = DC Motor
  BT1 = Bluetooth HC-06u [package=THT]

nets:
  N1: 부품1.D19/RX1, BT1.TXD
  N2: 부품1.D18/TX1, BT1.RXD
  N3: 부품1.D12_PWM, S1.ENA
  N4: 부품1.D11_PWM, S1.ENB
  N5: 부품1.D10_PWM, J3.pulse
  N6: 부품1.D9_PWM, J2.pulse
  N7: 부품1.D8_PWM, J1.pulse
  N8: 부품1.3V3, 부품3.3_3V
  GND: 부품1.GND, 부품3.GND
  N9: 부품1.D2_PWM, S1.IN1
  N10: 부품1.D3_PWM, S1.IN2
  N11: 부품1.D4_PWM, S1.IN3
  N12: 부품1.D5_PWM, S1.IN4
  N13: 부품1.D6_PWM, 부품2.DATAIN
  N14: 부품1.D7_PWM, J4.pin2
  N15: 부품1.D23, Keypad4x2.Pin1
  N16: 부품1.D25, Keypad4x2.Pin2
  N17: 부품1.D27, Keypad4x2.Pin3
  N18: 부품1.D29, Keypad4x2.Pin4
  N19: 부품1.D31, Keypad4x2.Pin5
  N20: 부품1.D33, Keypad4x2.Pin6
  N21: 부품1.D35, Keypad4x2.Pin7
  N22: 부품1.D37, Keypad4x2.Pin8
  N23: 부품1.D49, 부품3.RST
  N24: 부품1.D50, 부품3.MISO
  N25: 부품1.D51, 부품3.MOSI
  N26: 부품1.D52, 부품3.SCK
  N27: 부품1.D53, 부품3.SDA
  GND_2: 부품2.GND, J1.gnd, J2.gnd, J3.gnd, J4.pin1, S1.GND, BT1.GND
  VCC: 부품2.+5V, J1.vcc, J2.vcc, J3.vcc, S1.12V, S1.5V, BT1.VCC
  N28: S1.M1-01, F1.GND
  N29: S1.M1-02, F1.5V
  N30: S1.M2-01, M1.pin_2

custom parts:
  Keypad Membran 4x4: Membrane Keypad 4x4 Matrix
  NeoPixel Stick: Make your own little LED strip arrangement with this stick of NeoPixel LEDs. We crammed 8 of the tiny 5050 (5mm x 5mm) smart RGB LEDs onto a PCB with mounting holes and a chainable design. Use only one microcontroller pin to control as many as you can chain together! Each LED is addressable as the driver chip is inside the LED. Each one has ~18mA constant current drive so the color will be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
  RFID-RC522-v2: A simple China made RFID-RC522 Reader; do check the pin labels, as this is a MFRC522 based clone.
  H-Bridge with L298N: h-bridge
  Fan - Ventilador: Ventilador de 2 pines, se encuentra comunmente en computadoras de escritorio
  Bluetooth HC-06u: Bluetooth HC-06 - face up, pins down 16.5mm x 37.5mm PCB
